// Logisim project DDmini.circ as structural Verilog: 1 circuit, main circuit main
module main (
  input  [15:0] INSTRUCTION,
  input  START,
  input  RESET
);

  wire CLK_out, main_1_mw, main_1_ready;
  wire [3:0] main_1_addressout, main_1_dataout, ram_1_data;

  Clock CLK (.out(CLK_out));
  PROCESSOR_main main_1 (
    .IN(INSTRUCTION), .START(START), .RESET(RESET), .AddressOut(main_1_addressout), .DataOut(main_1_dataout),
    .DataIn(ram_1_data), .CLK(CLK_out), .READY(main_1_ready), .MW(main_1_mw));
  LED led_1 (.in(main_1_ready));
  RAM #(.addrWidth(4), .dataWidth(4), .bus("separate")) ram_1 (
    .addr(main_1_addressout), .din(main_1_dataout), .data(ram_1_data), .str(main_1_mw), .clk(CLK_out),
    .ld(1'b1));  // open: sel, clr
endmodule
