// Logisim project FUNCTION_UNIT.circ as structural Verilog: 1 circuit, main circuit main
// FUNIT
module main (
  input  [3:0] A,
  input  [3:0] B,
  input  [3:0] FS,
  output [3:0] F,
  output [2:0] PZN
);

  wire [3:0] adder_1_out, and_1_out, divider_1_out, multiplier_1_out, negator_1_out, not_1_out, or_1_out,
       shifter_1_out, shifter_2_out, shifter_3_out, subtractor_1_out;

  Adder #(.width(4)) adder_1 (.a(A), .b(B), .out(adder_1_out));  // open: cin, cout
  Subtractor #(.width(4)) subtractor_1 (.a(A), .b(B), .out(subtractor_1_out));  // open: bin, bout
  Multiplier #(.width(4)) multiplier_1 (.a(A), .b(B), .out(multiplier_1_out));  // open: cin, cout
  Divider #(.width(4)) divider_1 (.a(A), .b(B), .out(divider_1_out));  // open: upper, rem
  assign not_1_out = ~A;  // NOT_Gate not_1, 4 bits wide
  assign and_1_out = A & B;  // AND_Gate and_1, 4 bits wide
  assign or_1_out = B | A;  // OR_Gate or_1, 4 bits wide
  Negator #(.width(4)) negator_1 (.in(A), .out(negator_1_out));
  Shifter #(.width(4), .shift("lr")) shifter_1 (.in(A), .\dist (2'b01), .out(shifter_1_out));
  Shifter #(.width(4)) shifter_2 (.in(A), .\dist (2'b01), .out(shifter_2_out));
  Shifter #(.width(4), .shift("ar")) shifter_3 (.in(A), .\dist (2'b01), .out(shifter_3_out));
  Multiplexer #(.select(4), .width(4)) multiplexer_1 (
    .in0(4'b0000), .in1(4'b0001), .in2(A), .in3(B), .in4(adder_1_out), .in5(subtractor_1_out),
    .in6(multiplier_1_out), .in7(divider_1_out), .in8(not_1_out), .in9(and_1_out), .in10(or_1_out),
    .in11(negator_1_out), .in12(shifter_1_out), .in13(shifter_2_out), .in14(shifter_3_out), .out(F), .sel(FS));  // open: in15, en
  Comparator #(.width(4)) comparator_1 (.a(F), .b(4'b0000), .gt(PZN[2]), .eq(PZN[1]), .lt(PZN[0]));
endmodule
