// Logisim project LAB04_1.circ as structural Verilog: 1 circuit, main circuit main
module main (
  input  A1,
  input  A0,
  input  B1,
  input  B0,
  output C1,
  output C0
);

  Multiplexer #(.select(4), .disabled(0), .enable("false")) multiplexer_1 (
    .in0(1'b0), .in1(1'b0), .in2(1'b1), .in3(1'b1), .in4(1'b0), .in5(1'b0), .in6(1'b1), .in7(1'b1),
    .in8(1'b1), .in9(1'b1), .in10(1'b1), .in11(1'b1), .in12(1'b1), .in13(1'b1), .in14(1'b1), .in15(1'b1),
    .out(C1), .sel({A1, A0, B1, B0}));
  Multiplexer #(.select(4), .disabled(0), .enable("false")) multiplexer_2 (
    .in0(1'b0), .in1(1'b1), .in2(1'b0), .in3(1'b1), .in4(1'b1), .in5(1'b1), .in6(1'b0), .in7(1'b1),
    .in8(1'b0), .in9(1'b0), .in10(1'b0), .in11(1'b1), .in12(1'b1), .in13(1'b1), .in14(1'b1), .in15(1'b1),
    .out(C0), .sel({A1, A0, B1, B0}));

  // Notes on the sheet:
  //   A1+B1
  //   A0(A1+B1') + B0(A1'+B1)
endmodule
