// Logisim project LAB04_3.circ as structural Verilog: 1 circuit, main circuit main
module main (
  input  A1,
  input  A0,
  input  B1,
  input  B0,
  output C1,
  output C0
);

  wire nand_1_out, nand_2_out, nand_4_out, nand_5_out, nand_6_out, nand_7_out;

  nand nand_1 (nand_1_out, A1, A1);
  nand nand_2 (nand_2_out, B1, B1);
  nand nand_3 (C1, nand_1_out, nand_2_out);
  nand nand_4 (nand_4_out, A1, A0);
  nand nand_5 (nand_5_out, A0, nand_2_out);
  nand nand_6 (nand_6_out, nand_1_out, B0);
  nand nand_7 (nand_7_out, B1, B0);
  nand nand_8 (C0, nand_4_out, nand_5_out, nand_6_out, nand_7_out);

  // Notes on the sheet:
  //   A1'
  //   B1'
  //   A1+B1
  //   (A1A0)'
  //   (A0B1')'
  //   (A1'B0)'
  //   (B1B0)'
  //   A1'B0+A1A0+A0B1'+B1B0
endmodule
