// Logisim project LAB04_4.circ as structural Verilog: 1 circuit, main circuit oneBitMVS
// MVS
module oneBitMVS (
  input  [1:0] P,
  input  [1:0] I,
  output [1:0] O,
  output A
);

  wire and_1_out, and_2_out, and_3_out, and_4_out, and_5_out, and_6_out, and_7_out, and_8_out, and_9_out,
       and_10_out, not_1_out, not_2_out, not_3_out, not_4_out, not_5_out, not_6_out, not_7_out, not_8_out,
       not_9_out, not_10_out;

  not not_1 (not_1_out, P[0]);
  not not_2 (not_2_out, I[0]);
  not not_3 (not_3_out, P[0]);
  not not_4 (not_4_out, I[0]);
  not not_5 (not_5_out, P[1]);
  not not_6 (not_6_out, I[1]);
  not not_7 (not_7_out, P[1]);
  not not_8 (not_8_out, I[1]);
  not not_9 (not_9_out, P[1]);
  not not_10 (not_10_out, P[0]);
  and and_1 (and_1_out, not_1_out, I[1], not_2_out);
  and and_2 (and_2_out, P[1], not_3_out);
  and and_3 (and_3_out, P[1], I[1], not_4_out);
  and and_4 (and_4_out, not_5_out, not_6_out, I[0]);
  and and_5 (and_5_out, not_7_out, P[0]);
  and and_6 (and_6_out, P[0], not_8_out, I[0]);
  and and_7 (and_7_out, not_9_out, I[0]);
  and and_8 (and_8_out, not_10_out, I[1]);
  and and_9 (and_9_out, P[0], I[0]);
  and and_10 (and_10_out, P[1], I[1]);
  or or_1 (O[1], and_1_out, and_2_out, and_3_out);
  or or_2 (O[0], and_4_out, and_5_out, and_6_out);
  or or_3 (A, and_7_out, and_8_out, and_9_out, and_10_out);
endmodule
