// Logisim project LAB04_5.circ as structural Verilog: 1 circuit, main circuit main
module main (
  input  [3:0] A,
  input  [3:0] B,
  output [3:0] C
);

  wire [1:0] onebitmvs_1_o, onebitmvs_2_o, onebitmvs_3_o;

  oneBitMVS onebitmvs_1 (.A(C[3]), .P(2'b00), .I({B[3], A[3]}), .O(onebitmvs_1_o));
  oneBitMVS onebitmvs_2 (.A(C[2]), .P(onebitmvs_1_o), .I({B[2], A[2]}), .O(onebitmvs_2_o));
  oneBitMVS onebitmvs_3 (.A(C[1]), .P(onebitmvs_2_o), .I({B[1], A[1]}), .O(onebitmvs_3_o));
  oneBitMVS onebitmvs_4 (.A(C[0]), .P(onebitmvs_3_o), .I({B[0], A[0]}));  // open: O
endmodule
