// Logisim project LAB05_1.circ as structural Verilog: 1 circuit, main circuit main
module main (
  input  IN,
  output SHOT
);

  wire CLK_out, Q_q;

  Clock CLK (.out(CLK_out));
  or or_1 (SHOT, IN, Q_q);
  D_Flip_Flop Q (.clk(CLK_out), .D(SHOT), .Q(Q_q));  // open: Qn, preset, en, reset
endmodule
