// Logisim project LAB05_2.circ as structural Verilog: 1 circuit, main circuit main
module main (
  input  E,
  output T
);

  wire and_1_out, and_2_out, CLK_out, not_1_out, or_1_out, Q_qn;

  Clock CLK (.out(CLK_out));
  D_Flip_Flop Q (.clk(CLK_out), .D(or_1_out), .Q(T), .Qn(Q_qn));  // open: preset, en, reset
  not not_1 (not_1_out, E);
  and and_1 (and_1_out, not_1_out, T);
  and and_2 (and_2_out, Q_qn, E);
  or or_1 (or_1_out, and_1_out, and_2_out);

  // Notes on the sheet:
  //   E'Q
  //   EQ'
  //   E'Q+EQ'
endmodule
