// Logisim project LAB05_3.circ as structural Verilog: 1 circuit, main circuit main
module main (
  input  X,
  output Unlock
);

  wire and_1_out, and_2_out, and_3_out, and_5_out, CLK_out, not_1_out, or_1_out, or_2_out, Q0_q, Q0_qn, Q1_q,
       Q1_qn;

  Clock CLK (.out(CLK_out));
  not not_1 (not_1_out, X);
  D_Flip_Flop Q0 (.clk(CLK_out), .D(or_2_out), .Q(Q0_q), .Qn(Q0_qn));  // open: preset, en, reset
  D_Flip_Flop Q1 (.clk(CLK_out), .D(or_1_out), .Q(Q1_q), .Qn(Q1_qn));  // open: preset, en, reset
  and and_1 (and_1_out, X, Q0_qn);
  and and_2 (and_2_out, X, Q1_q);
  and and_3 (and_3_out, Q1_q, Q0_qn);
  and and_4 (Unlock, Q1_qn, Q0_q);
  and and_5 (and_5_out, Q1_q, not_1_out);
  or or_1 (or_1_out, and_1_out, and_2_out, and_3_out);
  or or_2 (or_2_out, Unlock, and_5_out);

  // Notes on the sheet:
  //   XQ0'
  //   XQ1
  //   Q0'Q1
  //   Q0Q1'
  //   X'Q1
endmodule
