// Logisim project LAB06.circ as structural Verilog: 1 circuit, main circuit main
module main (
  input  E,
  input  A,
  input  B,
  output V,
  output D
);

  wire and_1_out, and_2_out, and_3_out, and_4_out, and_5_out, and_6_out, and_7_out, and_8_out, and_9_out,
       and_10_out, and_11_out, and_12_out, and_13_out, and_14_out, and_15_out, and_16_out, clock_1_out,
       not_1_out, not_2_out, not_3_out, not_4_out, or_1_out, or_2_out, or_3_out, Q0_qn, Q1_q, Q1_qn, Q2_q,
       Q2_qn;

  Clock clock_1 (.out(clock_1_out));
  not not_1 (not_1_out, A);
  not not_2 (not_2_out, B);
  D_Flip_Flop Q2 (.clk(clock_1_out), .D(or_1_out), .Q(Q2_q), .Qn(Q2_qn));  // open: preset, en, reset
  D_Flip_Flop Q1 (.clk(clock_1_out), .D(or_2_out), .Q(Q1_q), .Qn(Q1_qn));  // open: preset, en, reset
  D_Flip_Flop Q0 (.clk(clock_1_out), .D(or_3_out), .Q(D), .Qn(Q0_qn));  // open: preset, en, reset
  not not_3 (not_3_out, E);
  and and_1 (and_1_out, not_2_out, D);
  and and_2 (and_2_out, not_1_out, Q2_qn, Q1_q);
  and and_3 (and_3_out, Q2_q, Q1_qn);
  and and_4 (and_4_out, Q2_q, D);
  and and_5 (and_5_out, B, Q2_qn, Q0_qn);
  and and_6 (and_6_out, A, Q1_qn);
  not not_4 (not_4_out, E);
  and and_7 (and_7_out, A, not_2_out, Q1_q, Q0_qn);
  and and_8 (and_8_out, A, Q2_q, Q1_q);
  and and_9 (and_9_out, A, B, Q2_qn, Q1_qn, Q0_qn);
  and and_10 (and_10_out, A, B, Q1_q, D);
  and and_11 (and_11_out, E, not_1_out, D);
  and and_12 (and_12_out, E, Q2_q, D);
  and and_13 (and_13_out, E, B, Q1_q);
  and and_14 (and_14_out, E, A, Q2_qn, Q1_qn, Q0_qn);
  or or_1 (or_1_out, not_3_out, and_1_out, and_2_out, and_3_out, and_4_out, and_5_out, and_6_out);
  or or_2 (or_2_out, not_4_out, and_7_out, and_8_out, and_9_out, and_10_out);
  or or_3 (or_3_out, and_11_out, and_12_out, and_13_out, and_14_out);
  and and_15 (and_15_out, Q2_q, Q1_qn);
  and and_16 (and_16_out, Q2_q, D);
  or or_4 (V, and_15_out, and_16_out);
endmodule
