// Logisim project LAB07_Moore.circ as structural Verilog: 1 circuit, main circuit main
module main (
  input  IN,
  output U
);

  wire and_2_out, and_3_out, and_4_out, and_5_out, and_6_out, and_7_out, and_8_out, and_9_out, and_10_out,
       and_11_out, and_12_out, and_13_out, and_14_out, and_15_out, clock_1_out, not_1_out, not_2_out,
       not_3_out, not_4_out, not_5_out, not_6_out, not_7_out, not_8_out, not_9_out, not_10_out, not_11_out,
       not_12_out, not_13_out, or_1_out, or_2_out, or_3_out, or_4_out, or_5_out, Q0_q, Q1_q, Q2_q;

  Clock clock_1 (.out(clock_1_out));
  D_Flip_Flop Q2 (.clk(clock_1_out), .D(or_5_out), .Q(Q2_q));  // open: Qn, preset, en, reset
  D_Flip_Flop Q1 (.clk(clock_1_out), .D(or_3_out), .Q(Q1_q));  // open: Qn, preset, en, reset
  D_Flip_Flop Q0 (.clk(clock_1_out), .D(or_4_out), .Q(Q0_q));  // open: Qn, preset, en, reset
  not not_1 (not_1_out, Q0_q);
  not not_2 (not_2_out, IN);
  not not_3 (not_3_out, Q0_q);
  not not_4 (not_4_out, IN);
  not not_5 (not_5_out, Q2_q);
  not not_6 (not_6_out, Q1_q);
  not not_7 (not_7_out, Q1_q);
  not not_8 (not_8_out, Q0_q);
  not not_9 (not_9_out, Q2_q);
  not not_10 (not_10_out, Q1_q);
  not not_11 (not_11_out, Q2_q);
  not not_12 (not_12_out, Q1_q);
  and and_1 (U, Q2_q, Q1_q);
  and and_2 (and_2_out, not_1_out, IN);
  and and_3 (and_3_out, Q0_q, not_2_out);
  and and_4 (and_4_out, not_3_out, not_4_out);
  and and_5 (and_5_out, Q0_q, IN);
  and and_6 (and_6_out, Q0_q, IN);
  and and_7 (and_7_out, not_5_out, not_6_out, Q0_q);
  and and_8 (and_8_out, Q2_q, not_7_out, not_8_out);
  and and_9 (and_9_out, Q2_q, Q1_q, Q0_q);
  and and_10 (and_10_out, Q0_q, IN);
  and and_11 (and_11_out, not_9_out, not_10_out, IN);
  and and_12 (and_12_out, not_11_out, Q1_q, Q0_q);
  and and_13 (and_13_out, Q2_q, not_12_out, IN);
  or or_1 (or_1_out, and_2_out, and_3_out);
  not not_13 (not_13_out, Q1_q);
  or or_2 (or_2_out, and_4_out, and_5_out);
  or or_3 (or_3_out, and_6_out, and_7_out, and_8_out, and_9_out);
  or or_4 (or_4_out, and_10_out, and_11_out, and_12_out, and_13_out);
  and and_14 (and_14_out, Q1_q, or_1_out);
  or or_5 (or_5_out, and_14_out, and_15_out);
  and and_15 (and_15_out, Q2_q, not_13_out, or_2_out);
endmodule
