// Logisim project LAB08.circ as structural Verilog: 1 circuit, main circuit main
module main (
  input  GO,
  input  [3:0] IN,
  input  [1:0] F,
  output [3:0] OUT
);

  wire and_1_out, CLK_out, Q0_qn;
  wire [3:0] adder_1_out, multiplexer_1_out, multiplier_1_out, subtractor_1_out;

  Clock CLK (.out(CLK_out));
  Adder #(.width(4)) adder_1 (.a(OUT), .b(IN), .out(adder_1_out));  // open: cin, cout
  Subtractor #(.width(4)) subtractor_1 (.a(OUT), .b(IN), .out(subtractor_1_out));  // open: bin, bout
  Multiplier #(.width(4)) multiplier_1 (.a(OUT), .b(IN), .out(multiplier_1_out));  // open: cin, cout
  D_Flip_Flop Q0 (.clk(CLK_out), .D(GO), .Qn(Q0_qn));  // open: Q, preset, en, reset
  and and_1 (and_1_out, Q0_qn, GO);
  Multiplexer #(.select(2), .width(4)) multiplexer_1 (
    .in0(IN), .in1(adder_1_out), .in2(subtractor_1_out), .in3(multiplier_1_out), .out(multiplexer_1_out),
    .sel(F));  // open: en
  Register #(.width(4)) register_1 (.D(multiplexer_1_out), .en(and_1_out), .Q(OUT), .clk(CLK_out));  // open: clr
endmodule
