// Logisim project LAB09.circ as structural Verilog: 1 circuit, main circuit main
module main (
  input  in_1,
  input  in_2
);

  wire clock_1_out, DP_reset, DP_switch, or_1_out;
  wire [1:0] CU_sel;
  wire [2:0] DP_flr, DP_hlr;

  Clock clock_1 (.out(clock_1_out));
  or or_1 (or_1_out, in_2, DP_reset);
  CU CU (.CARDETECTED(in_1), .RESET(or_1_out), .SWITCH(DP_switch), .SEL(CU_sel), .CLK(clock_1_out));
  DP DP (.SEL(CU_sel), .FLR(DP_flr), .HLR(DP_hlr), .SWITCH(DP_switch), .CLK(clock_1_out), .RESET(DP_reset));
  LED led_1 (.in(DP_flr[2]));
  LED led_2 (.in(DP_flr[1]));
  LED led_3 (.in(DP_flr[0]));
  LED led_4 (.in(DP_hlr[2]));
  LED led_5 (.in(DP_hlr[1]));
  LED led_6 (.in(DP_hlr[0]));
  LED led_7 (.in(DP_flr[2]));
  LED led_8 (.in(DP_flr[1]));
  LED led_9 (.in(DP_flr[0]));
  LED led_10 (.in(DP_hlr[2]));
  LED led_11 (.in(DP_hlr[1]));
  LED led_12 (.in(DP_hlr[0]));
endmodule
