// Logisim project LAB09_control.circ as structural Verilog: 1 circuit, main circuit CU
module CU (
  input  CARDETECTED,
  input  RESET,
  input  SWITCH,
  input  CLK,
  output [1:0] SEL
);

  wire and_1_out, and_2_out, and_3_out, and_4_out, d_ff_1_q, d_ff_2_q, nor_1_out, not_1_out, not_2_out,
       not_3_out, not_4_out, not_5_out, or_1_out, or_2_out;

  D_Flip_Flop d_ff_1 (.clk(CLK), .D(CARDETECTED), .Q(d_ff_1_q), .en(nor_1_out));  // open: Qn, preset, reset
  not not_1 (not_1_out, RESET);
  not not_2 (not_2_out, RESET);
  or or_1 (or_1_out, SWITCH, d_ff_2_q);
  and and_1 (and_1_out, d_ff_1_q, not_1_out, SWITCH);
  or or_2 (or_2_out, and_1_out, and_2_out, and_4_out);
  and and_2 (and_2_out, d_ff_1_q, not_2_out, d_ff_2_q);
  D_Flip_Flop d_ff_2 (.clk(CLK), .D(and_3_out), .Q(d_ff_2_q));  // open: Qn, preset, en, reset
  and and_3 (and_3_out, or_1_out, not_3_out);
  not not_3 (not_3_out, or_2_out);
  Counter #(.width(2), .max('h3)) counter_1 (
    .load(RESET), .D(2'b00), .count(or_2_out), .Q(SEL), .clk(CLK));  // open: carry, clr
  not not_4 (not_4_out, CARDETECTED);
  nor nor_1 (nor_1_out, SEL[0], SEL[1]);
  not not_5 (not_5_out, SEL[0]);
  and and_4 (and_4_out, not_5_out, SEL[1], not_4_out);
endmodule
