// Logisim project LAB09_datapath.circ as structural Verilog: 1 circuit, main circuit DP
module DP (
  input  [1:0] SEL,
  input  CLK,
  output RESET,
  output [2:0] FLR,
  output [2:0] HLR,
  output SWITCH
);

  wire comparator_1_eq, comparator_2_gt, comparator_3_eq, comparator_4_gt, comparator_4_lt, comparator_5_gt,
       comparator_5_lt, not_1_out;
  wire [1:0] bitadder_1_out, bitadder_2_out, register_1_q;
  wire [3:0] counter_1_q, multiplexer_2_out;
  wire [5:0] multiplexer_1_out;

  Comparator #(.width(2)) comparator_1 (.a(SEL), .b(register_1_q), .eq(comparator_1_eq));  // open: gt, lt
  Register #(.width(2)) register_1 (.D(SEL), .Q(register_1_q), .clk(CLK));  // open: en, clr
  not not_1 (not_1_out, comparator_1_eq);
  Multiplexer #(.select(2), .width(6)) multiplexer_1 (
    .in0(6'b001100), .in1(6'b010100), .in2(6'b100001), .in3(6'b100010), .out(multiplexer_1_out), .sel(SEL));  // open: en
  Counter #(.width(4), .max('he)) counter_1 (
    .load(not_1_out), .D(4'b0000), .count(comparator_1_eq), .Q(counter_1_q), .clk(CLK));  // open: carry, clr
  Register #(.width(3)) u_FLR (.D(multiplexer_1_out[2:0]), .Q(FLR), .clk(CLK));  // open: en, clr
  Register #(.width(3)) u_HLR (.D(multiplexer_1_out[5:3]), .Q(HLR), .clk(CLK));  // open: en, clr
  Comparator #(.width(4), .mode("unsigned")) comparator_2 (
    .a(counter_1_q), .b(multiplexer_2_out), .gt(comparator_2_gt));  // open: eq, lt
  Multiplexer #(.width(4)) multiplexer_2 (
    .in0(4'b1101), .in1(4'b0000), .out(multiplexer_2_out), .sel(SEL[0]));  // open: en
  and and_1 (SWITCH, comparator_2_gt, comparator_1_eq);
  BitAdder #(.width(3)) bitadder_1 (.in0(HLR), .out(bitadder_1_out));
  BitAdder #(.width(3)) bitadder_2 (.in0(FLR), .out(bitadder_2_out));
  Comparator #(.width(3)) comparator_3 (.a(HLR), .b(FLR), .eq(comparator_3_eq));  // open: gt, lt
  Comparator #(.width(2)) comparator_4 (
    .a(bitadder_1_out), .b(2'b01), .gt(comparator_4_gt), .lt(comparator_4_lt));  // open: eq
  Comparator #(.width(2)) comparator_5 (
    .a(bitadder_2_out), .b(2'b01), .gt(comparator_5_gt), .lt(comparator_5_lt));  // open: eq
  or or_1 (RESET, comparator_4_gt, comparator_4_lt, comparator_5_gt, comparator_5_lt, comparator_3_eq);
endmodule
