// Logisim project LAB11_DATAPATH.circ as structural Verilog: 1 circuit, main circuit main
// DATA
module main (
  input  [2:0] D_Address,
  input  RegfileWrite,
  input  CLK,
  input  [2:0] A_Address,
  input  [2:0] B_Address,
  input  [3:0] ConstIn,
  input  MuxB,
  input  [3:0] FunctionSelect,
  input  [3:0] DataIn,
  input  MuxF,
  output [3:0] AddrOut,
  output [3:0] DataOut,
  output [2:0] PZN
);

  wire [3:0] main_1_bout, main_2_f, multiplexer_2_out;

  REGFILE_8x4_main main_1 (
    .Din(multiplexer_2_out), .LD(RegfileWrite), .AA(A_Address), .DA(D_Address), .BA(B_Address),
    .Aout(AddrOut), .Bout(main_1_bout), .CLK(CLK));
  Multiplexer #(.width(4), .enable("false")) multiplexer_1 (
    .in0(main_1_bout), .in1(ConstIn), .out(DataOut), .sel(MuxB));
  FUNCTION_UNIT_main main_2 (.A(AddrOut), .B(DataOut), .FS(FunctionSelect), .F(main_2_f), .PZN(PZN));
  Multiplexer #(.width(4), .enable("false")) multiplexer_2 (
    .in0(main_2_f), .in1(DataIn), .out(multiplexer_2_out), .sel(MuxF));
endmodule
