// Logisim project LAB12_CONTROLUNIT.circ as structural Verilog: 1 circuit, main circuit main
// CONTROL
module main (
  input  [15:0] IN,
  input  [2:0] PZN,
  input  RESET,
  input  CLK,
  input  START,
  output [3:0] CONSTANT,
  output [15:0] CONTROL,
  output MW,
  output READY
);

  wire and_1_out, and_2_out, and_3_out, and_4_out, and_5_out, not_1_out, or_1_out, or_2_out;
  wire [2:0] register_1_q;
  wire [7:0] counter_1_q, multiplexer_1_out;
  wire [17:17] rom_1_data;

  Register #(.width(3)) register_1 (.D(PZN), .Q(register_1_q), .clk(CLK));  // open: en, clr
  and and_1 (and_1_out, register_1_q[2], CONTROL[14]);
  and and_2 (and_2_out, register_1_q[1], CONTROL[13]);
  and and_3 (and_3_out, register_1_q[0], CONTROL[12]);
  and and_4 (and_4_out, or_2_out, rom_1_data[17]);
  Multiplexer #(.width(8), .enable("false")) multiplexer_1 (
    .in0(CONTROL[11:4]), .in1({IN[15:12], 4'b0000}), .out(multiplexer_1_out), .sel(and_5_out));
  or or_1 (or_1_out, and_4_out, and_5_out);
  not not_1 (not_1_out, or_1_out);
  or or_2 (or_2_out, and_1_out, and_2_out, and_3_out);
  Counter counter_1 (
    .load(or_1_out), .D(multiplexer_1_out), .count(not_1_out), .Q(counter_1_q), .clk(CLK), .clr(RESET));  // open: carry
  Multiplexer #(.select(2), .width(4), .enable("false")) multiplexer_2 (
    .in0(4'b0000), .in1(IN[11:8]), .in2(IN[7:4]), .in3(IN[3:0]), .out(CONSTANT), .sel(CONTROL[10:9]));
  Comparator comparator_1 (.a(counter_1_q), .b({8{1'b0}}), .eq(READY));  // open: gt, lt
  and and_5 (and_5_out, READY, START);
  ROM #(.dataWidth(18)) rom_1 (.addr(counter_1_q), .data({rom_1_data[17], MW, CONTROL}));  // open: sel

  // Notes on the sheet:
  //   contents of rom_1 (hex, n*v repeats v):
  //   27000 15*0 1231 11400 27000 13*0 1231 1433 2103 10200 27000 11*0 1231 1433 1635 2103 4105 2445 10400
  //   27000 8*0 1231 1433 1635 2103 4105 2455 10400 27000 8*0 1231 1433 20135 2103 4105 2465 10400 2700
  //   8*0 1231 1433 2103 20c3 10200 27000 10*0 1231 1433 2103 2083 10200 27000 10*0 1231 1433 1635 2103
  //   4105 2493 10200 27000 8*0 1635 4105 4025 22950 27000 1231 1433 2103 10200 27000 6*0 1231 1433 1635
  //   2103 4105 2453 22aa0 13 10200 27000 10200 27000 4*0 1433 1635 2029 2103 4105 40c5 2457 22ba0 18400
  //   27000 1231 13 10200 27000
endmodule
