// Logisim project Lab04_2.circ as structural Verilog: 1 circuit, main circuit main
module main (
  input  A1,
  input  A0,
  input  B1,
  input  B0,
  output C1,
  output C0
);

  wire multiplexer_2_out, multiplexer_3_out, multiplexer_4_out, multiplexer_5_out;

  Multiplexer #(.disabled(0), .enable("false")) multiplexer_1 (.in0(B1), .in1(A1), .out(C1), .sel(A1));
  Multiplexer #(.disabled(0), .enable("false")) multiplexer_2 (
    .in0(1'b1), .in1(1'b0), .out(multiplexer_2_out), .sel(A1));
  Multiplexer #(.disabled(0), .enable("false")) multiplexer_3 (
    .in0(1'b1), .in1(1'b0), .out(multiplexer_3_out), .sel(B1));
  Multiplexer #(.disabled(0)) multiplexer_4 (
    .in0(multiplexer_2_out), .in1(B1), .out(multiplexer_4_out), .sel(B1), .en(B0));
  Multiplexer #(.disabled(0)) multiplexer_5 (
    .in0(multiplexer_3_out), .in1(A1), .out(multiplexer_5_out), .sel(A1), .en(A0));
  Multiplexer #(.disabled(0), .enable("false")) multiplexer_6 (
    .in0(multiplexer_4_out), .in1(multiplexer_5_out), .out(C0), .sel(multiplexer_5_out));

  // Notes on the sheet:
  //   A1'
  //   B1'
  //   A1+B1
  //   B0(A1'+B1)
  //   A0(A1+B1')
  //   A0(A1+B1')+B0(A1+B1)
endmodule
