// Logisim project MICROPROCESSOR.circ as structural Verilog: 1 circuit, main circuit main
// PROCESSOR
module main (
  input  [15:0] IN,
  input  START,
  input  [3:0] DataIn,
  input  RESET,
  input  CLK,
  output [3:0] AddressOut,
  output [3:0] DataOut,
  output MW,
  output READY
);

  wire [2:0] main_2_pzn;
  wire [3:0] main_1_constant;
  wire [15:0] main_1_control;

  LAB12_CONTROLUNIT_main main_1 (
    .IN(IN), .PZN(main_2_pzn), .RESET(RESET), .CLK(CLK), .START(START), .CONSTANT(main_1_constant),
    .CONTROL(main_1_control), .MW(MW), .READY(READY));
  LAB11_DATAPATH_main main_2 (
    .D_Address(main_1_control[3:1]), .RegfileWrite(main_1_control[0]), .CLK(CLK),
    .A_Address(main_1_control[15:13]), .B_Address(main_1_control[11:9]), .ConstIn(main_1_constant),
    .MuxB(main_1_control[12]), .FunctionSelect(main_1_control[7:4]), .MuxF(main_1_control[8]),
    .AddrOut(AddressOut), .DataOut(DataOut), .PZN(main_2_pzn), .DataIn(DataIn));
endmodule
