// Logisim project REGFILE_8x4.circ as structural Verilog: 1 circuit, main circuit main
// REGFILE
module main (
  input  [3:0] Din,
  input  LD,
  input  [2:0] AA,
  input  [2:0] DA,
  input  CLK,
  input  [2:0] BA,
  output [3:0] Aout,
  output [3:0] Bout
);

  wire and_1_out, and_2_out, and_3_out, and_4_out, and_5_out, and_6_out, and_7_out, and_8_out,
       decoder_1_out0, decoder_1_out1, decoder_1_out2, decoder_1_out3, decoder_1_out4, decoder_1_out5,
       decoder_1_out6, decoder_1_out7;
  wire [3:0] register_1_q, register_2_q, register_3_q, register_4_q, register_5_q, register_6_q,
       register_7_q, register_8_q;

  Decoder #(.select(3)) decoder_1 (
    .out0(decoder_1_out0), .out1(decoder_1_out1), .out2(decoder_1_out2), .out3(decoder_1_out3),
    .out4(decoder_1_out4), .out5(decoder_1_out5), .out6(decoder_1_out6), .out7(decoder_1_out7), .sel(DA));  // open: en
  and and_1 (and_1_out, decoder_1_out0, LD);
  and and_2 (and_2_out, decoder_1_out2, LD);
  and and_3 (and_3_out, decoder_1_out4, LD);
  and and_4 (and_4_out, decoder_1_out6, LD);
  and and_5 (and_5_out, LD, decoder_1_out1);
  and and_6 (and_6_out, LD, decoder_1_out3);
  and and_7 (and_7_out, LD, decoder_1_out5);
  and and_8 (and_8_out, LD, decoder_1_out7);
  Register #(.width(4)) register_1 (.D(Din), .en(and_1_out), .Q(register_1_q), .clk(CLK), .clr(1'b0));
  Register #(.width(4)) register_2 (.D(Din), .en(and_2_out), .Q(register_2_q), .clk(CLK), .clr(1'b0));
  Register #(.width(4)) register_3 (.D(Din), .en(and_3_out), .Q(register_3_q), .clk(CLK), .clr(1'b0));
  Register #(.width(4)) register_4 (.D(Din), .en(and_4_out), .Q(register_4_q), .clk(CLK), .clr(1'b0));
  Register #(.width(4)) register_5 (.D(Din), .en(and_5_out), .Q(register_5_q), .clk(CLK), .clr(1'b0));
  Register #(.width(4)) register_6 (.D(Din), .en(and_6_out), .Q(register_6_q), .clk(CLK), .clr(1'b0));
  Register #(.width(4)) register_7 (.D(Din), .en(and_7_out), .Q(register_7_q), .clk(CLK), .clr(1'b0));
  Register #(.width(4)) register_8 (.D(Din), .en(and_8_out), .Q(register_8_q), .clk(CLK), .clr(1'b0));
  Multiplexer #(.select(3), .width(4), .enable("false")) multiplexer_1 (
    .in0(register_1_q), .in1(register_5_q), .in2(register_2_q), .in3(register_6_q), .in4(register_3_q),
    .in5(register_7_q), .in6(register_4_q), .in7(register_8_q), .out(Aout), .sel(AA));
  Multiplexer #(.select(3), .width(4), .enable("false")) multiplexer_2 (
    .in0(register_1_q), .in1(register_5_q), .in2(register_2_q), .in3(register_6_q), .in4(register_3_q),
    .in5(register_7_q), .in6(register_4_q), .in7(register_8_q), .out(Bout), .sel(BA));
endmodule
